# Fritzing sketch mainboard (saved by Fritzing 0.9.3b)
circuit board: 3cm x 6.5cm
circuit board: 7.80366cm x 6.58223cm
breadboards: 1

parts:
  Nano = Arduino Nano (Rev3.0)
  Q2 = PNP-Transistor [package="TO92 [THT]"]
  Q3 = NPN-Transistor [package="TO92 [THT]"]
  Q4 = NPN-Transistor [package="TO92 [THT]"]
  R1 = Resistor [tolerance=±5% resistance=10k package=THT]
  R3 = Resistor [tolerance=±5% resistance=10k package=THT]
  R4 = Resistor [tolerance=±5% resistance=10k package=THT]
  R2 = Resistor [tolerance=±5% resistance=10k package=THT]
  J1 = female pin header, 2 pins [form="♀ (female)"]
  Q5 = PNP-Transistor [package="TO92 [THT]"]
  Q6 = PNP-Transistor [package="TO92 [THT]"]
  Q7 = NPN-Transistor [package="TO92 [THT]"]
  Q8 = NPN-Transistor [package="TO92 [THT]"]
  R8 = Resistor [tolerance=±5% resistance=10k package=THT]
  R6 = Resistor [tolerance=±5% resistance=10k package=THT]
  R7 = Resistor [tolerance=±5% resistance=10k package=THT]
  R5 = Resistor [tolerance=±5% resistance=10k package=THT]
  J2 = female pin header, 2 pins [form="♀ (female)"]
  Shutdown = Pushbutton [package="[THT]"]
  MinUMU9v5 = mystery part, 5 pins [chip_label=?]
  POWER = USB Connectors [package=usb-minib-nostop]  # not connected
  USB = USB Connectors [package=usb-minib-nostop]  # not connected
  HDMI = USB+SHIELD [package=usb-b-pth]  # not connected
  J3 = female pin header, 3 pins [form="♀ (female)"]
  J4 = female pin header, 3 pins [form="♀ (female)"]
  D1 = male pin header, 2 pins [form="♂ (male)"]
  Q1 = PNP-Transistor [package="TO92 [THT]"]
  D3 = male pin header, 2 pins [form="♂ (male)"]
  D2 = male pin header, 2 pins [form="♂ (male)"]
  D4 = male pin header, 2 pins [form="♂ (male)"]
  D7 = male pin header, 2 pins [form="♂ (male)"]
  D5 = male pin header, 2 pins [form="♂ (male)"]
  D8 = male pin header, 2 pins [form="♂ (male)"]
  D9 = male pin header, 2 pins [form="♂ (male)"]
  HC-SR04 = hc-sr04
  R9 = Resistor [tolerance=±5% resistance=1k package=THT]
  R10 = Resistor [tolerance=±5% resistance=2.2k package=THT]
  GPIO = Generic double row male header - 40 pins [form="♂ (male)" package=THT]
  5v = female pin header, 2 pins [form="♀ (female)"]
  10v = female pin header, 2 pins [form="♀ (female)"]
  C2 = Ceramic Capacitor [capacitance=100nF package="100 mil [THT, multilayer]"]
  C1 = Electrolytic Capacitor [capacitance=1µF package="100 mil [THT, electrolytic]"]
  C3 = Ceramic Capacitor [capacitance=100nF package="100 mil [THT, multilayer]"]
  R11 = Resistor [tolerance=±5% resistance=1k package=THT]
  R12 = Resistor [tolerance=±5% resistance=2.2k package=THT]

nets:
  N1: Nano.GND, Q3.E, Q4.E, Q7.E, Q8.E, Shutdown.Pin_1, Shutdown.Pin_2, Shutdown.Pin_3, Shutdown.Pin_4, J3.pin2, J4.pin2, D3.pin2, D4.pin2, D7.pin2, D9.pin2, GPIO.pin39, GPIO.pin38, GPIO.pin6, 5v.pin2, 10v.pin2, C2.1, C1.-, C3.0, R12.Pin_0
  N2: Nano.D2, J4.pin1
  N3: Nano.D3, J3.pin1
  N4: Nano.D5, R1.Pin_1, R3.Pin_0
  N5: Nano.D6, R4.Pin_0, R2.Pin_1
  N6: Nano.D9, R7.Pin_0, R5.Pin_1
  N7: Nano.D10, R8.Pin_0, R6.Pin_1
  VIN: Nano.VIN, J3.pin3, J4.pin3, HC-SR04.VCC, GPIO.pin4, 5v.pin1, C2.0, C1.+, C3.1
  N8: Nano.A5, MinUMU9v5.pin1, GPIO.pin5
  N9: Nano.A4, MinUMU9v5.pin2, GPIO.pin3
  N10: Nano.A0, R11.Pin_0, R12.Pin_1
  N11: Q2.E, Q5.E, Q6.E, D1.pin1, Q1.E, D2.pin1, D5.pin1, D8.pin1, 10v.pin1, R11.Pin_1
  N12: Q2.B, R2.Pin_0
  N13: Q2.C, Q4.C, J1.pin1, D2.pin2, D4.pin1
  N14: Q3.B, R3.Pin_1
  N15: Q3.C, J1.pin2, D1.pin2, Q1.C, D3.pin1
  N16: Q4.B, R4.Pin_1
  N17: R1.Pin_0, Q1.B
  N18: Q5.B, R5.Pin_0
  N19: Q5.C, Q7.C, J2.pin2, D7.pin1, D5.pin2
  N20: Q6.B, R6.Pin_0
  N21: Q6.C, Q8.C, J2.pin1, D8.pin2, D9.pin1
  N22: Q7.B, R7.Pin_1
  N23: Q8.B, R8.Pin_1
  N24: MinUMU9v5.pin3, GPIO.pin14
  N25: MinUMU9v5.pin5, GPIO.pin17
  N26: HC-SR04.Trig, GPIO.pin22
  N27: HC-SR04.Echo, R9.Pin_0
  N28: HC-SR04.GND, GPIO.pin30
  N29: R9.Pin_1, R10.Pin_1, GPIO.pin18
  N30: R10.Pin_0, GPIO.pin20

custom parts:
  Generic double row male header - 40 pins: Generic double row male header
